# Fritzing sketch IRRemoteSetup (saved by Fritzing 0.9.10b)

parts:
  Part1 = Arduino Uno (Rev3)
  IR1 = TSOP312.., 314.. [package=THT]

nets:
  N1: Part1.D10_PWM/SS, IR1.GND
  N2: Part1.5V, IR1.Data
  N3: Part1.GND, IR1.Vs

// code stored in the sketch: control-light-with-remote-controller.ino
#include <IRremote.h> // https://github.com/z3t0/Arduino-IRremote library needs to be included

int bright;
int before;
int out = 10;        // connect your LED to pin 9 
int steps = 5;       // dimmer steps, vary those to increase/decrease the steps between full brightness and turned off
int RECV_PIN = 3;    // data out of IR receiver connects to pin 3

IRrecv irrecv(RECV_PIN);
decode_results results;

void setup() {
    Serial.begin(9600);   // starts serial communication
    irrecv.enableIRIn();  // start the receiver
    before = 0;           // LED is turned off
    bright = 255;         // brightness value is at maximum (255)
    
    pinMode(out, OUTPUT);
}

void loop() {
  if (irrecv.decode(&results)) {
    //Serial.println(results.value); // Print pressed key code
    
    // Code to turn the LED ON/OFF
    if (results.value==284153895) {
        if(before==0) { // if the LED was turned off, then we turn it on 
            Serial.println("TURN ON"); // Print pressed key code
            
            digitalWrite(out, HIGH);
            before=1; //LED is now turned on
        }
        else {
            Serial.println("TURN OFF"); // Print pressed key code
          
            digitalWrite(out, LOW); // if the LED was turned on, then we turn it off
            before=0;
            bright=255; 
        }
    }

    // Code to decrease the brightness
    if (results.value==284098815 && before==1) {
        Serial.println("DECREASE");
      
        if(bright-255/steps<0) { 
            analogWrite(out, bright);
        }
        else {
            bright=bright-255/steps;
            analogWrite(out, bright);
        }
    }
  
    // Code to increase the brightness
    if (results.value==284139615 && before==1) {
          Serial.println("INCREASE");

          if(bright+255/steps>255) {
              analogWrite(out, bright);
          }
          else{    
              bright=bright+255/steps;
              analogWrite(out, bright);
          }
    }
  
    irrecv.resume();
  }
}
